# Fritzing sketch schematics (saved by Fritzing 1.0.1rc)

parts:
  Raspberry_Pi_4B = Raspberry Pi 4B
  PSU = DC Power [voltage=12V]
  Logic_level_shifter = IC, DIP package, 14 pins [chip_label=74AHCT125N]
  SK6812_RGBW_stripled = JST-B3P-VH [part_number=JST-B3P-VH package=THT]

nets:
  N1: Raspberry_Pi_4B.5V, Logic_level_shifter.pin14
  N2: Raspberry_Pi_4B.GND, PSU.V-, Logic_level_shifter.pin1, Logic_level_shifter.pin7, SK6812_RGBW_stripled.pin3
  N3: Raspberry_Pi_4B.GPIO18, Logic_level_shifter.pin2
  N4: PSU.V+, SK6812_RGBW_stripled.pin1
  N5: Logic_level_shifter.pin3, SK6812_RGBW_stripled.pin2
